// Logisim project LOGISIM.circ as structural Verilog: 11 circuits, main circuit main
module main (
  input  [1:0] in_1,
  input  [23:0] in_2,
  input  [23:0] in_3,
  output [23:0] out_4,
  output ZERO,
  output NEGETIVE,
  output OVERFLOW,
  output CARRY
);

  L_24_bit_alu l_24_bit_alu_1 (
    .control_1(in_1[1]), .Control_0(in_1[0]), .in_3(in_2), .in_4(in_3), .out_5(out_4), .Zero(ZERO),
    .NEGETIVE(NEGETIVE), .CARRY(CARRY), .OVERFLOW(OVERFLOW));

  // Notes on the sheet:
  //   A
  //   B
  //   RESULT
endmodule

module andgets24bit (
  input  [23:0] in_1,
  input  [23:0] in_2,
  output [23:0] out_3
);

  and and_1 (out_3[12], in_1[12], in_2[12]);
  and and_2 (out_3[0], in_1[0], in_2[0]);
  and and_3 (out_3[1], in_1[1], in_2[1]);
  and and_4 (out_3[2], in_1[2], in_2[2]);
  and and_5 (out_3[3], in_1[3], in_2[3]);
  and and_6 (out_3[4], in_1[4], in_2[4]);
  and and_7 (out_3[5], in_1[5], in_2[5]);
  and and_8 (out_3[6], in_1[6], in_2[6]);
  and and_9 (out_3[7], in_1[7], in_2[7]);
  and and_10 (out_3[8], in_1[8], in_2[8]);
  and and_11 (out_3[9], in_1[9], in_2[9]);
  and and_12 (out_3[10], in_1[10], in_2[10]);
  and and_13 (out_3[11], in_1[11], in_2[11]);
  and and_14 (out_3[13], in_1[13], in_2[13]);
  and and_15 (out_3[14], in_1[14], in_2[14]);
  and and_16 (out_3[15], in_1[15], in_2[15]);
  and and_17 (out_3[16], in_1[16], in_2[16]);
  and and_18 (out_3[17], in_1[17], in_2[17]);
  and and_19 (out_3[18], in_2[18], in_1[18]);
  and and_20 (out_3[19], in_1[19], in_2[19]);
  and and_21 (out_3[20], in_1[20], in_2[20]);
  and and_22 (out_3[21], in_1[21], in_2[21]);
  and and_23 (out_3[22], in_1[22], in_2[22]);
  and and_24 (out_3[23], in_1[23], in_2[23]);

  // Notes on the sheet:
  //   A
  //   B
  //   RESULT
endmodule

module ORGATE24BIT (
  input  [23:0] in_1,
  input  [23:0] in_2,
  output [23:0] out_3
);

  or or_1 (out_3[12], in_1[12], in_2[12]);
  or or_2 (out_3[0], in_1[0], in_2[0]);
  or or_3 (out_3[1], in_1[1], in_2[1]);
  or or_4 (out_3[2], in_1[2], in_2[2]);
  or or_5 (out_3[3], in_1[3], in_2[3]);
  or or_6 (out_3[4], in_1[4], in_2[4]);
  or or_7 (out_3[5], in_1[5], in_2[5]);
  or or_8 (out_3[6], in_1[6], in_2[6]);
  or or_9 (out_3[7], in_1[7], in_2[7]);
  or or_10 (out_3[8], in_1[8], in_2[8]);
  or or_11 (out_3[9], in_1[9], in_2[9]);
  or or_12 (out_3[10], in_1[10], in_2[10]);
  or or_13 (out_3[11], in_1[11], in_2[11]);
  or or_14 (out_3[13], in_1[13], in_2[13]);
  or or_15 (out_3[14], in_1[14], in_2[14]);
  or or_16 (out_3[15], in_1[15], in_2[15]);
  or or_17 (out_3[16], in_1[16], in_2[16]);
  or or_18 (out_3[17], in_1[17], in_2[17]);
  or or_19 (out_3[18], in_2[18], in_1[18]);
  or or_20 (out_3[19], in_1[19], in_2[19]);
  or or_21 (out_3[20], in_1[20], in_2[20]);
  or or_22 (out_3[21], in_1[21], in_2[21]);
  or or_23 (out_3[22], in_1[22], in_2[22]);
  or or_24 (out_3[23], in_1[23], in_2[23]);

  // Notes on the sheet:
  //   A
  //   B
  //   result
endmodule

module ONEBITADDER (
  input  in_1,
  input  in_2,
  input  in_3,
  output SUM,
  output CARRY
);

  wire and_1_out, and_2_out, xor_1_out;

  and and_1 (and_1_out, in_3, in_2);
  xor xor_1 (xor_1_out, in_2, in_3);
  xor xor_2 (SUM, in_1, xor_1_out);
  and and_2 (and_2_out, in_1, xor_1_out);
  or or_1 (CARRY, and_2_out, and_1_out);
endmodule

module ADDER24BIT (
  input  CARRY_IN,
  input  [23:0] in_2,
  input  [23:0] in_3,
  output [23:0] out_4,
  output CARRY_OUT
);

  wire adder_1_cout, adder_2_cout, adder_3_cout, adder_4_cout, adder_5_cout, adder_6_cout, adder_7_cout,
       adder_8_cout, adder_9_cout, adder_10_cout, adder_11_cout, adder_12_cout, adder_13_cout, adder_14_cout,
       adder_15_cout, adder_16_cout, adder_17_cout, adder_18_cout, adder_19_cout, adder_20_cout,
       adder_21_cout, adder_22_cout, adder_23_cout;

  Adder #(.width(1)) adder_1 (.a(in_2[0]), .b(in_3[0]), .out(out_4[0]), .cin(CARRY_IN), .cout(adder_1_cout));
  Adder #(.width(1)) adder_2 (.a(in_2[1]), .b(in_3[1]), .out(out_4[1]), .cin(adder_1_cout), .cout(adder_2_cout));
  Adder #(.width(1)) adder_3 (.a(in_2[2]), .b(in_3[2]), .out(out_4[2]), .cin(adder_2_cout), .cout(adder_3_cout));
  Adder #(.width(1)) adder_4 (.a(in_2[3]), .b(in_3[3]), .out(out_4[3]), .cin(adder_3_cout), .cout(adder_4_cout));
  Adder #(.width(1)) adder_5 (.a(in_2[4]), .b(in_3[4]), .out(out_4[4]), .cin(adder_4_cout), .cout(adder_5_cout));
  Adder #(.width(1)) adder_6 (.a(in_2[5]), .b(in_3[5]), .out(out_4[5]), .cin(adder_5_cout), .cout(adder_6_cout));
  Adder #(.width(1)) adder_7 (.a(in_2[6]), .b(in_3[6]), .out(out_4[6]), .cin(adder_6_cout), .cout(adder_7_cout));
  Adder #(.width(1)) adder_8 (.a(in_2[7]), .b(in_3[7]), .out(out_4[7]), .cin(adder_7_cout), .cout(adder_8_cout));
  Adder #(.width(1)) adder_9 (.a(in_2[8]), .b(in_3[8]), .out(out_4[8]), .cin(adder_8_cout), .cout(adder_9_cout));
  Adder #(.width(1)) adder_10 (.a(in_2[9]), .b(in_3[9]), .out(out_4[9]), .cin(adder_9_cout), .cout(adder_10_cout));
  Adder #(.width(1)) adder_11 (.a(in_2[10]), .b(in_3[10]), .out(out_4[10]), .cin(adder_10_cout), .cout(adder_11_cout));
  Adder #(.width(1)) adder_12 (.a(in_2[11]), .b(in_3[11]), .out(out_4[11]), .cin(adder_11_cout), .cout(adder_12_cout));
  Adder #(.width(1)) adder_13 (.a(in_2[12]), .b(in_3[12]), .out(out_4[12]), .cin(adder_12_cout), .cout(adder_13_cout));
  Adder #(.width(1)) adder_14 (.a(in_2[13]), .b(in_3[13]), .out(out_4[13]), .cin(adder_13_cout), .cout(adder_14_cout));
  Adder #(.width(1)) adder_15 (.a(in_2[14]), .b(in_3[14]), .out(out_4[14]), .cin(adder_14_cout), .cout(adder_15_cout));
  Adder #(.width(1)) adder_16 (.a(in_2[15]), .b(in_3[15]), .out(out_4[15]), .cin(adder_15_cout), .cout(adder_16_cout));
  Adder #(.width(1)) adder_17 (.a(in_2[16]), .b(in_3[16]), .out(out_4[16]), .cin(adder_16_cout), .cout(adder_17_cout));
  Adder #(.width(1)) adder_18 (.a(in_2[17]), .b(in_3[17]), .out(out_4[17]), .cin(adder_17_cout), .cout(adder_18_cout));
  Adder #(.width(1)) adder_19 (.a(in_2[18]), .b(in_3[18]), .out(out_4[18]), .cin(adder_18_cout), .cout(adder_19_cout));
  Adder #(.width(1)) adder_20 (.a(in_2[19]), .b(in_3[19]), .out(out_4[19]), .cin(adder_19_cout), .cout(adder_20_cout));
  Adder #(.width(1)) adder_21 (.a(in_2[20]), .b(in_3[20]), .out(out_4[20]), .cin(adder_20_cout), .cout(adder_21_cout));
  Adder #(.width(1)) adder_22 (.a(in_2[21]), .b(in_3[21]), .out(out_4[21]), .cin(adder_21_cout), .cout(adder_22_cout));
  Adder #(.width(1)) adder_23 (.a(in_2[22]), .b(in_3[22]), .out(out_4[22]), .cin(adder_22_cout), .cout(adder_23_cout));
  Adder #(.width(1)) adder_24 (.a(in_2[23]), .b(in_3[23]), .out(out_4[23]), .cin(adder_23_cout), .cout(CARRY_OUT));

  // Notes on the sheet:
  //   RESULT
endmodule

module L_24BITADDER (
  input  in_1,
  input  A0,
  input  B0,
  input  A1,
  input  B1,
  input  A2,
  input  B2,
  input  A3,
  input  B3,
  input  A4,
  input  B4,
  input  A5,
  input  B5,
  input  A6,
  input  B6,
  input  A7,
  input  B7,
  input  A8,
  input  B8,
  input  A9,
  input  B9,
  input  A10,
  input  B10,
  input  A11,
  input  B11,
  input  A12,
  input  B12,
  input  A13,
  input  B13,
  input  A14,
  input  B14,
  input  A15,
  input  B15,
  input  A16,
  input  B16,
  input  A17,
  input  B17,
  input  A18,
  input  B18,
  input  A19,
  input  B19,
  input  A20,
  input  B20,
  input  A21,
  input  B21,
  input  A22,
  input  B22,
  input  A23,
  input  B23,
  output RES_0,
  output RES_1,
  output RES_2,
  output RES_3,
  output RES_4,
  output RES_5,
  output RES_6,
  output RES_7,
  output RES_8,
  output RES_9,
  output RES_10,
  output RES_11,
  output RES_12,
  output RES_13,
  output RES_14,
  output RES_15,
  output RES_16,
  output RES_17,
  output RES_18,
  output RES_19,
  output RES_20,
  output RES_21,
  output RES_22,
  output RES_23,
  output CARRY_OUT
);

  wire adder_1_cout, adder_2_cout, adder_3_cout, adder_4_cout, adder_5_cout, adder_6_cout, adder_7_cout,
       adder_8_cout, adder_9_cout, adder_10_cout, adder_11_cout, adder_12_cout, adder_13_cout, adder_14_cout,
       adder_15_cout, adder_16_cout, adder_17_cout, adder_18_cout, adder_19_cout, adder_20_cout,
       adder_21_cout, adder_22_cout, adder_23_cout;

  Adder #(.width(1)) adder_1 (.a(A0), .b(B0), .out(RES_0), .cin(in_1), .cout(adder_1_cout));
  Adder #(.width(1)) adder_2 (.a(A1), .b(B1), .out(RES_1), .cin(adder_1_cout), .cout(adder_2_cout));
  Adder #(.width(1)) adder_3 (.a(A2), .b(B2), .out(RES_2), .cin(adder_2_cout), .cout(adder_3_cout));
  Adder #(.width(1)) adder_4 (.a(A3), .b(B3), .out(RES_3), .cin(adder_3_cout), .cout(adder_4_cout));
  Adder #(.width(1)) adder_5 (.a(A4), .b(B4), .out(RES_4), .cin(adder_4_cout), .cout(adder_5_cout));
  Adder #(.width(1)) adder_6 (.a(A5), .b(B5), .out(RES_5), .cin(adder_5_cout), .cout(adder_6_cout));
  Adder #(.width(1)) adder_7 (.a(A6), .b(B6), .out(RES_6), .cin(adder_6_cout), .cout(adder_7_cout));
  Adder #(.width(1)) adder_8 (.a(A7), .b(B7), .out(RES_7), .cin(adder_7_cout), .cout(adder_8_cout));
  Adder #(.width(1)) adder_9 (.a(A8), .b(B8), .out(RES_8), .cin(adder_8_cout), .cout(adder_9_cout));
  Adder #(.width(1)) adder_10 (.a(A9), .b(B9), .out(RES_9), .cin(adder_9_cout), .cout(adder_10_cout));
  Adder #(.width(1)) adder_11 (.a(A10), .b(B10), .out(RES_10), .cin(adder_10_cout), .cout(adder_11_cout));
  Adder #(.width(1)) adder_12 (.a(A11), .b(B11), .out(RES_11), .cin(adder_11_cout), .cout(adder_12_cout));
  Adder #(.width(1)) adder_13 (.a(A12), .b(B12), .out(RES_12), .cin(adder_12_cout), .cout(adder_13_cout));
  Adder #(.width(1)) adder_14 (.a(A13), .b(B13), .out(RES_13), .cin(adder_13_cout), .cout(adder_14_cout));
  Adder #(.width(1)) adder_15 (.a(A14), .b(B14), .out(RES_14), .cin(adder_14_cout), .cout(adder_15_cout));
  Adder #(.width(1)) adder_16 (.a(A15), .b(B15), .out(RES_15), .cin(adder_15_cout), .cout(adder_16_cout));
  Adder #(.width(1)) adder_17 (.a(A16), .b(B16), .out(RES_16), .cin(adder_16_cout), .cout(adder_17_cout));
  Adder #(.width(1)) adder_18 (.a(A17), .b(B17), .out(RES_17), .cin(adder_17_cout), .cout(adder_18_cout));
  Adder #(.width(1)) adder_19 (.a(A18), .b(B18), .out(RES_18), .cin(adder_18_cout), .cout(adder_19_cout));
  Adder #(.width(1)) adder_20 (.a(A19), .b(B19), .out(RES_19), .cin(adder_19_cout), .cout(adder_20_cout));
  Adder #(.width(1)) adder_21 (.a(A20), .b(B20), .out(RES_20), .cin(adder_20_cout), .cout(adder_21_cout));
  Adder #(.width(1)) adder_22 (.a(A21), .b(B21), .out(RES_21), .cin(adder_21_cout), .cout(adder_22_cout));
  Adder #(.width(1)) adder_23 (.a(A22), .b(B22), .out(RES_22), .cin(adder_22_cout), .cout(adder_23_cout));
  Adder #(.width(1)) adder_24 (.a(A23), .b(B23), .out(RES_23), .cin(adder_23_cout), .cout(CARRY_OUT));

  // Notes on the sheet:
  //   CARRY IN
endmodule

module ZEROCHECK (
  input  [23:0] in_1,
  output OUTPUT
);

  or or_1 (OUTPUT, in_1[0], in_1[1], in_1[2], in_1[3], in_1[4], in_1[5], in_1[6], in_1[7], in_1[8], in_1[9], in_1[10], in_1[11], in_1[12], in_1[13], in_1[14], in_1[15], in_1[16], in_1[17], in_1[18], in_1[19], in_1[20], in_1[21], in_1[22], in_1[23]);

  // Notes on the sheet:
  //   INPUT
endmodule

module XOR_24_BIT (
  input  in_1,
  input  [23:0] in_2,
  output [23:0] out_3
);

  wire [23:0] bit_extender_1_out;

  assign bit_extender_1_out = {{23{in_1}}, in_1};  // Bit_Extender bit_extender_1
  assign out_3 = bit_extender_1_out ^ in_2;  // XOR_Gate xor_1, 24 bits wide
endmodule

module ADD_SUB (
  input  in_1,
  input  [23:0] in_2,
  input  [23:0] in_3,
  output [23:0] out_4,
  output out_5,
  output OVERFLOW
);

  wire and_1_out, and_2_out, l_23_bit_out_1__23_bit, l_23_bit_out_2__23_bit, l_23_bit_out_3__23_bit,
       not_1_out, not_2_out, not_3_out;
  wire [23:0] xor_24_bit_1_out_3;

  or or_1 (OVERFLOW, and_1_out, and_2_out);
  L_23_BIT_OUT l_23_bit_out_1 (.in_1(in_2), ._23_BIT(l_23_bit_out_1__23_bit));
  not not_1 (not_1_out, l_23_bit_out_1__23_bit);
  XOR_24_BIT xor_24_bit_1 (.in_1(in_1), .in_2(in_3), .out_3(xor_24_bit_1_out_3));
  L_23_BIT_OUT l_23_bit_out_2 (.in_1(in_3), ._23_BIT(l_23_bit_out_2__23_bit));
  not not_2 (not_2_out, l_23_bit_out_2__23_bit);
  ADDER24BIT adder24bit_1 (.CARRY_IN(in_1), .in_2(in_2), .in_3(xor_24_bit_1_out_3), .out_4(out_4), .CARRY_OUT(out_5));
  and and_1 (and_1_out, l_23_bit_out_1__23_bit, not_3_out, l_23_bit_out_2__23_bit);
  and and_2 (and_2_out, not_2_out, l_23_bit_out_3__23_bit, not_1_out);
  not not_3 (not_3_out, l_23_bit_out_3__23_bit);
  L_23_BIT_OUT l_23_bit_out_3 (.in_1(out_4), ._23_BIT(l_23_bit_out_3__23_bit));

  // Notes on the sheet:
  //   A
  //   B
  //   SUB
  //   CARRY
endmodule

module L_23_BIT_OUT (
  input  [23:0] in_1,
  output _23_BIT
);


  assign _23_BIT = in_1[23];

  // Notes on the sheet:
  //   INPUT
endmodule

module L_24_bit_alu (
  input  control_1,
  input  Control_0,
  input  [23:0] in_3,
  input  [23:0] in_4,
  output [23:0] out_5,
  output Zero,
  output NEGETIVE,
  output CARRY,
  output OVERFLOW
);

  wire zerocheck_1_output;
  wire [23:0] add_sub_1_out_4, andgets24bit_1_out_3, multiplexer_1_out, orgate24bit_1_out_3;

  andgets24bit andgets24bit_1 (.in_1(in_3), .in_2(in_4), .out_3(andgets24bit_1_out_3));
  ORGATE24BIT orgate24bit_1 (.in_1(in_3), .in_2(in_4), .out_3(orgate24bit_1_out_3));
  ADD_SUB add_sub_1 (
    .in_1(Control_0), .in_2(in_3), .in_3(in_4), .out_4(add_sub_1_out_4), .out_5(CARRY), .OVERFLOW(OVERFLOW));
  Multiplexer #(.width(24)) multiplexer_1 (
    .in0(andgets24bit_1_out_3), .in1(orgate24bit_1_out_3), .out(multiplexer_1_out), .sel(Control_0));
  Multiplexer #(.width(24)) multiplexer_2 (
    .in0(multiplexer_1_out), .in1(add_sub_1_out_4), .out(out_5), .sel(control_1));
  L_23_BIT_OUT l_23_bit_out_1 (.in_1(out_5), ._23_BIT(NEGETIVE));
  ZEROCHECK zerocheck_1 (.in_1(out_5), .OUTPUT(zerocheck_1_output));
  not not_1 (Zero, zerocheck_1_output);

  // Notes on the sheet:
  //   A
  //   B
  //   Result
endmodule
